# Fritzing sketch Untitled Sketch 2 (saved by Fritzing 0.9.3b)
breadboards: 1

parts:
  R1 = Resistor [tolerance=±5% resistance=10k package=THT]
  Част1 = Arduino Nano (Rev3.0)
  DHT1 = DHT11 Humitidy and Temperature Sensor

nets:
  5V: R1.Pin_0, Част1.5V, DHT1.VDD
  N1: R1.Pin_1, Част1.D2, DHT1.DATA
  GND: Част1.GND, DHT1.GND

notes:
  D2 pin
  +5v
  GND
  10K

custom parts:
  DHT11 Humitidy and Temperature Sensor: DHT11 Humidity and Temperature Sensor
